# Fritzing sketch IsClock (saved by Fritzing 0.9.0b)
circuit board: 10cm x 5cm
breadboards: 2

parts:
  A1 = atmega328 [package=dip]
  C2 = Capacitor [package=cap-pth-small2]
  C1 = Capacitor [package=cap-pth-small2]
  Y1 = CRYSTAL [package=crystal-smd-10.5x4.8-2pin]
  J1 = female pin header, 2 pins [form="♀ (female)"]
  D1 = Rectifier Diode [part_number=1N4001 package="300 mil [THT]"]
  LCD2 = LCD screen

nets:
  N1: A1.D2, LCD2.DB7
  N2: A1.D3_(PWM), LCD2.DB6
  N3: A1.D4, LCD2.DB5
  VCC: A1.VCC, A1.AVCC, A1.AREF, D1.cathode, LCD2.VDD
  GND: A1.GND, C2.2, C1.2, J1.pin2, LCD2.VSS, LCD2.V0, LCD2.R/W
  N4: A1.XLAT1, C1.1, Y1.1
  N5: A1.XLAT2, C2.1, Y1.2
  N6: A1.D5_(PWM), LCD2.DB4
  N7: A1.D11_(PWM), LCD2.E
  N8: A1.D12, LCD2.RS
  N9: J1.pin1, D1.anode

notes:
  Capacitors: 22 pF
  Crystal: 16 MHz
